# Fritzing sketch alici_fritzing (saved by Fritzing 0.9.3b)
breadboards: 1

parts:
  LCD1 = LCD screen
  Parça1 = Arduino Uno (Rev3)
  Parça2 = NRF24L01+ Breakout Board
  U1 = POT [package=pot_alpha_rv16af-20]
  J1 = Piezo Speaker
  LED1 = smd LED [color="Red (633nm)" package="0603 [SMD]"]
  LED2 = smd LED [color="Red (633nm)" package="0603 [SMD]"]
  LED3 = smd LED [color="Red (633nm)" package="0603 [SMD]"]
  LED4 = smd LED [color="Red (633nm)" package="0603 [SMD]"]
  R1 = Resistor [tolerance=±5% resistance=220 package="0402 [SMD]"]
  TTP223B1 = TTP223B Capacitive Touch Sensor Module

nets:
  GND: LCD1.VSS, LCD1.R/W, LCD1.LED-, Parça1.GND, Parça2.GND, U1.A, J1.pin1, LED1.cathode, LED2.cathode, LED3.cathode, LED4.cathode, TTP223B1.GND
  VDD: LCD1.VDD, Parça1.5V, U1.E, R1.Pin_0, TTP223B1.VCC
  N1: LCD1.V0, U1.S
  N2: LCD1.RS, Parça1.D7
  N3: LCD1.E, Parça1.D6_PWM
  N4: LCD1.DB4, Parça1.D5_PWM
  N5: LCD1.DB5, Parça1.D4
  N6: LCD1.DB6, Parça1.D3_PWM
  N7: LCD1.DB7, Parça1.D2
  N8: LCD1.LED+, R1.Pin_1
  N9: Parça1.A0, TTP223B1.SIG
  N10: Parça1.A1, J1.pin2
  N11: Parça1.A2, LED4.anode
  N12: Parça1.A3, LED3.anode
  N13: Parça1.A4/SDA, LED2.anode
  N14: Parça1.A5/SCL, LED1.anode
  N15: Parça1.D8, Parça2.CS
  N16: Parça1.D9_PWM, Parça2.CE
  N17: Parça1.D11_PWM/MOSI, Parça2.MOSI
  N18: Parça1.D12/MISO, Parça2.MISO
  N19: Parça1.D13/SCK, Parça2.SCK
  3V3: Parça1.3V3, Parça2.VCC

custom parts:
  TTP223B Capacitive Touch Sensor Module: The TTP223B capacitive touch sensor module uses the TTP223B IC. The appropriate voltage is approximately 2 to 5.5 volts.
