# Fritzing sketch alici_fritzing2 (saved by Fritzing 0.9.3b)
breadboards: 1

parts:
  LCD1 = LCD screen
  Parça1 = Arduino Uno (Rev3)
  Parça2 = NRF24L01+ Breakout Board
  J1 = Piezo Speaker
  LED1 = smd LED [color="Red (633nm)" package="0603 [SMD]"]
  LED2 = smd LED [color="Red (633nm)" package="0603 [SMD]"]
  LED3 = smd LED [color="Red (633nm)" package="0603 [SMD]"]
  LED4 = smd LED [color="Red (633nm)" package="0603 [SMD]"]
  TTP223B1 = TTP223B Capacitive Touch Sensor Module
  LCM1602_IIC1 = LCM1602 IIC [part_number="LCM1602 IIC" chip_label="LCM1602 IIC" package="DIP (Dual Inline) [THT]"]
  J2 = Basic Servo

nets:
  VSS: LCD1.VSS, LCM1602_IIC1.VSS
  VDD: LCD1.VDD, LCM1602_IIC1.VDD
  N1: LCD1.V0, LCM1602_IIC1.V0
  N2: LCD1.RS, LCM1602_IIC1.RS
  N3: LCD1.R/W, LCM1602_IIC1.RW
  N4: LCD1.E, LCM1602_IIC1.E
  N5: LCD1.DB0, LCM1602_IIC1.D0
  N6: LCD1.DB1, LCM1602_IIC1.D1
  N7: LCD1.DB2, LCM1602_IIC1.D2
  N8: LCD1.DB3, LCM1602_IIC1.D3
  N9: LCD1.DB4, LCM1602_IIC1.D4
  N10: LCD1.DB5, LCM1602_IIC1.D5
  N11: LCD1.DB6, LCM1602_IIC1.D6
  N12: LCD1.DB7, LCM1602_IIC1.D7
  N13: LCD1.LED+, LCM1602_IIC1.A
  N14: LCD1.LED-, LCM1602_IIC1.K
  VCC: Parça1.A4/SDA, Parça1.A5/SCL, Parça1.5V, TTP223B1.VCC, LCM1602_IIC1.VCC, LCM1602_IIC1.SDA, LCM1602_IIC1.SCL, J2.vcc
  N15: Parça1.D8, Parça2.CS
  N16: Parça1.D9_PWM, Parça2.CE
  N17: Parça1.D10_PWM/SS, J2.pulse
  N18: Parça1.D11_PWM/MOSI, Parça2.MOSI
  N19: Parça1.D12/MISO, Parça2.MISO
  N20: Parça1.D13/SCK, Parça2.SCK
  GND: Parça1.GND, Parça2.GND, J1.pin1, LED1.cathode, LED2.cathode, LED3.cathode, LED4.cathode, TTP223B1.GND, LCM1602_IIC1.GND, J2.gnd
  N21: Parça1.D2, TTP223B1.SIG
  N22: Parça1.D3_PWM, J1.pin2
  N23: Parça1.D4, LED4.anode
  N24: Parça1.D5_PWM, LED3.anode
  N25: Parça1.D6_PWM, LED2.anode
  N26: Parça1.D7, LED1.anode
  3V3: Parça1.3V3, Parça2.VCC
  N27: LCM1602_IIC1.LED_A, LCM1602_IIC1.LED_B

custom parts:
  TTP223B Capacitive Touch Sensor Module: The TTP223B capacitive touch sensor module uses the TTP223B IC. The appropriate voltage is approximately 2 to 5.5 volts.
  LCM1602 IIC: I2C-Module to use a 1602 or 2004 LCD on with the wire.h libory Serial LCD Modul
