# Fritzing sketch verici_fritzing (saved by Fritzing 0.9.3b)
breadboards: 2

parts:
  Parça1 = Arduino Uno (Rev3)
  Parça2 = NRF24L01+ Breakout Board
  Parça3 = Barometric Pressure Sensor - BMP180 Breakout (GY-68)
  Mod1 = KY-015 Temperature & Humidity Sensor Module [package="Breakout board"]
  M1 = fc-51 [package=THT]
  7_Segment2 = 7 Segment Display
  R1 = Resistor [tolerance=±5% resistance=220 package="0805 [SMD]"]
  R2 = Resistor [tolerance=±5% resistance=220 package="0805 [SMD]"]

nets:
  N1: Parça1.A0, 7_Segment2.Segment_D
  N2: Parça1.A1, 7_Segment2.Segment_E
  N3: Parça1.A3, M1.pin1
  N4: Parça1.A4/SDA, Parça3.SDA
  N5: Parça1.A5/SCL, Parça3.SCL
  N6: Parça1.D8, Parça2.CS
  N7: Parça1.D9_PWM, Parça2.CE
  N8: Parça1.D10_PWM/SS, Mod1.S
  N9: Parça1.D11_PWM/MOSI, Parça2.MOSI
  N10: Parça1.D12/MISO, Parça2.MISO
  N11: Parça1.D13/SCK, Parça2.SCK
  GND: Parça1.GND, Parça2.GND, Parça3.GND, Mod1.-, M1.pin2, R1.Pin_1, R2.Pin_1
  N12: Parça1.D2, 7_Segment2.Segment_DP
  N13: Parça1.D3_PWM, 7_Segment2.Segment_A
  N14: Parça1.D4, 7_Segment2.Segment_B
  N15: Parça1.D5_PWM, 7_Segment2.Segment_C
  N16: Parça1.D6_PWM, 7_Segment2.Segment_F
  N17: Parça1.D7, 7_Segment2.Segment_G
  VCC: Parça1.3V3, Parça2.VCC, Parça3.VCC
  5V: Parça1.5V, Mod1.Vin, M1.pin3
  N18: 7_Segment2.common_cathode, R1.Pin_0, R2.Pin_0

custom parts:
  KY-015 Temperature & Humidity Sensor Module: KY-015 temperature and humidity sensor module, provides a low-latency serial interface to measure humidity and temperature.
